# Fritzing sketch Bluetooth Light Switch Schematic (saved by Fritzing 0.9.3b)
circuit board: 8.46667cm x 5.64444cm
breadboards: 1

parts:
  Part1 = Arduino Nano (Rev3.0)
  R2 = Resistor [tolerance=±5% resistance=3.3k package=THT]
  R1 = Resistor [tolerance=±5% resistance=2.2k package=THT]
  S1 = Round Pushbutton
  R3 = Resistor [tolerance=±5% resistance=10k package=THT]
  Q1 = Basic FET N-Channel [part_number=RFP12N10L package="TO220 [THT]"]
  U1 = RELAY [package=OJ]
  Part2 = Bluetooth HM-10
  D1 = Rectifier Diode [part_number=1N4001 package="300 mil [THT]"]

nets:
  GND: Part1.GND, R2.Pin_1, S1.leg1, R3.Pin_1, Q1.source, Part2.GND
  N1: Part1.D3, R3.Pin_0, Q1.gate
  N2: Part1.D4, Part2.VCC
  N3: Part1.D7, Part2.STATE
  N4: Part1.D8, Part2.TXD
  N5: Part1.D9, R1.Pin_1
  N6: Part1.D12/MISO, S1.leg0
  9V: Part1.VIN, U1.COIL2, D1.cathode
  N7: R2.Pin_0, R1.Pin_0, Part2.RXD
  N8: Q1.drain, U1.COIL1, D1.anode

custom parts:
  Bluetooth HM-10: Modified by droopymiller
